# Fritzing sketch Untitled Sketch (saved by Fritzing 0.9.3b)

parts:
  A1 = u-blox NEO-6M GPS Breakout
  Part1 = Arduino Nano (Rev3.0)
  GSM_SIM_GPSR_SMS_SIM900_SIM1 = SIM800L [package=THT]
  ANT1 = Antenna
  D1 = SOLAR-IXYS [package=solarbit-12x1]
  U1 = LIPO-110mAh [package=lipo-110]
  S1 = Round Pushbutton

nets:
  N1: A1.Pin_3, Part1.D7
  N2: A1.Pin_4, Part1.D6
  N3: Part1.GND, S1.leg1
  N4: Part1.A3, GSM_SIM_GPSR_SMS_SIM900_SIM1.SIM_TXD
  N5: Part1.A2, GSM_SIM_GPSR_SMS_SIM900_SIM1.SIM_RXD
  N6: GSM_SIM_GPSR_SMS_SIM900_SIM1.VDD, ANT1.antenna_lead
  N7: D1.A, U1.+
  N8: D1.C, U1.-
